// Logisim project multiplexador.circ as structural Verilog: 1 circuit, main circuit Multiplexador
module Multiplexador (
  input  E2,
  input  E1,
  input  E0,
  output S0,
  output S1,
  output S2,
  output S3,
  output S4,
  output S5,
  output S6,
  output S7
);

  wire not_1_out, not_2_out, not_3_out;

  not not_1 (not_1_out, E0);
  not not_2 (not_2_out, E1);
  not not_3 (not_3_out, E2);
  and and_1 (S0, not_1_out, not_2_out, not_3_out);
  and and_2 (S1, not_1_out, not_2_out, E2);
  and and_3 (S2, not_1_out, E1, not_3_out);
  and and_4 (S3, not_1_out, E1, E2);
  and and_5 (S4, E0, not_2_out, not_3_out);
  and and_6 (S5, E0, not_2_out, E2);
  and and_7 (S6, E0, E1, not_3_out);
  and and_8 (S7, E0, E1, E2);
endmodule
